# Fritzing sketch Distributed_Snake_BB-diagram (saved by Fritzing 1.0.6)
breadboards: 4

parts:
  Pico/Pico2_Mod_1 = Raspberry Pi Pico or Pico 2
  C1 = Ceramic Capacitor [capacitance=100nF voltage=35V package="100 mil [THT, multilayer]"]
  C2 = Ceramic Capacitor [capacitance=100nF voltage=35V package="100 mil [THT, multilayer]"]
  R1 = TRIMPOT [maximum_resistance=10kΩ knob_status=50% power=0.5W package=3362u-2]
  S2 = Pushbutton [package=THT]
  J1 = female pin header, 1 pin [form="♀ (female)"]
  J2 = female pin header, 1 pin [form="♀ (female)"]
  J3 = female pin header, 1 pin [form="♀ (female)"]
  J5 = VGA Adapter Board [package=THT]
  TRS2 = Audio Jack (TRS) 3.5mm [package="PG203J [THT]"]
  S3 = Pushbutton [package=THT]
  Power_plug1 = Power plug
  C3 = Electrolytic Capacitor [capacitance=47µF voltage=35V package="100 mil [THT, electrolytic]"]
  Pico/Pico2_Mod_2 = Raspberry Pi Pico or Pico 2
  Pico/Pico2_Mod_3 = Raspberry Pi Pico or Pico 2
  D2 = Schottky Diode [part_number=1N5817 package="300 mil [THT]"]
  D3 = Schottky Diode [part_number=1N5817 package="300 mil [THT]"]
  D4 = Schottky Diode [part_number=1N5817 package="300 mil [THT]"]
  D5 = Schottky Diode [part_number=1N5817 package="300 mil [THT]"]
  Pico/Pico2_Mod_4 = Raspberry Pi Pico or Pico 2
  Pico/Pico2_Mod_5 = Raspberry Pi Pico or Pico 2
  C4 = Ceramic Capacitor [capacitance=100nF voltage=35V package="100 mil [THT, multilayer]"]
  C5 = Ceramic Capacitor [capacitance=100nF voltage=35V package="100 mil [THT, multilayer]"]
  C6 = Ceramic Capacitor [capacitance=100nF voltage=35V package="100 mil [THT, multilayer]"]
  C7 = Ceramic Capacitor [capacitance=100nF voltage=35V package="100 mil [THT, multilayer]"]
  D6 = Schottky Diode [part_number=1N5817 package="300 mil [THT]"]

nets:
  N1: Pico/Pico2_Mod_1.pin_1, J3.pin1
  N2: Pico/Pico2_Mod_1.pin_2, J2.pin1
  GND: Pico/Pico2_Mod_1.pin_3, Pico/Pico2_Mod_1.pin_8, Pico/Pico2_Mod_1.pin_13, Pico/Pico2_Mod_1.pin_18, Pico/Pico2_Mod_1.pin_23, Pico/Pico2_Mod_1.pin_28, Pico/Pico2_Mod_1.pin_33, Pico/Pico2_Mod_1.pin_36, Pico/Pico2_Mod_1.pin_38, Pico/Pico2_Mod_1.pin_42, C1.1, C2.1, R1.CCW, R1.CW, S2.leg1, J1.pin1, J5.GND, TRS2.Sleeve, S3.leg1, Power_plug1.GND, C3.-, Pico/Pico2_Mod_2.pin_3, Pico/Pico2_Mod_2.pin_8, Pico/Pico2_Mod_2.pin_13, Pico/Pico2_Mod_2.pin_18, Pico/Pico2_Mod_2.pin_23, Pico/Pico2_Mod_2.pin_28, Pico/Pico2_Mod_2.pin_33, Pico/Pico2_Mod_2.pin_38, Pico/Pico2_Mod_3.pin_3, Pico/Pico2_Mod_3.pin_8, Pico/Pico2_Mod_3.pin_13, Pico/Pico2_Mod_3.pin_18, Pico/Pico2_Mod_3.pin_23, Pico/Pico2_Mod_3.pin_28, Pico/Pico2_Mod_3.pin_33, Pico/Pico2_Mod_3.pin_38, Pico/Pico2_Mod_3.pin_42, Pico/Pico2_Mod_4.pin_3, Pico/Pico2_Mod_4.pin_8, Pico/Pico2_Mod_4.pin_13, Pico/Pico2_Mod_4.pin_18, Pico/Pico2_Mod_4.pin_23, Pico/Pico2_Mod_4.pin_28, Pico/Pico2_Mod_4.pin_33, Pico/Pico2_Mod_4.pin_38, Pico/Pico2_Mod_4.pin_42, Pico/Pico2_Mod_5.pin_3, Pico/Pico2_Mod_5.pin_8, Pico/Pico2_Mod_5.pin_13, Pico/Pico2_Mod_5.pin_18, Pico/Pico2_Mod_5.pin_23, Pico/Pico2_Mod_5.pin_28, Pico/Pico2_Mod_5.pin_33, Pico/Pico2_Mod_5.pin_38, C4.0, C4.1, C5.0, C6.1, C7.0
  N3: Pico/Pico2_Mod_1.pin_14, J5.HSYNC
  N4: Pico/Pico2_Mod_1.pin_15, J5.VSYNC
  N5: Pico/Pico2_Mod_1.pin_16, J5.LGREEN
  N6: Pico/Pico2_Mod_1.pin_17, J5.HGREEN
  N7: Pico/Pico2_Mod_1.pin_19, J5.BLUE
  N8: Pico/Pico2_Mod_1.pin_20, J5.RED
  N9: Pico/Pico2_Mod_1.pin_21, Pico/Pico2_Mod_2.pin_21, Pico/Pico2_Mod_3.pin_21, Pico/Pico2_Mod_4.pin_21, Pico/Pico2_Mod_5.pin_21
  N10: Pico/Pico2_Mod_1.pin_22, Pico/Pico2_Mod_2.pin_22
  N11: Pico/Pico2_Mod_1.pin_24, Pico/Pico2_Mod_2.pin_24, Pico/Pico2_Mod_3.pin_24, Pico/Pico2_Mod_4.pin_24, Pico/Pico2_Mod_5.pin_24
  N12: Pico/Pico2_Mod_1.pin_25, Pico/Pico2_Mod_2.pin_25, Pico/Pico2_Mod_3.pin_25, Pico/Pico2_Mod_4.pin_25, Pico/Pico2_Mod_5.pin_25
  N13: Pico/Pico2_Mod_1.pin_26, Pico/Pico2_Mod_4.pin_22
  N14: Pico/Pico2_Mod_1.pin_27, Pico/Pico2_Mod_5.pin_22
  N15: Pico/Pico2_Mod_1.pin_29, Pico/Pico2_Mod_3.pin_22
  N16: Pico/Pico2_Mod_1.pin_30, S3.leg0, Pico/Pico2_Mod_2.pin_30, Pico/Pico2_Mod_3.pin_30, Pico/Pico2_Mod_4.pin_30, Pico/Pico2_Mod_5.pin_30
  N17: Pico/Pico2_Mod_1.pin_31, S2.leg0
  N18: Pico/Pico2_Mod_1.pin_32, R1.WIPER
  N19: Pico/Pico2_Mod_1.pin_39, D6.cathode
  N20: C1.0, C2.0, Power_plug1.VCC, C3.+, D2.anode, D3.anode, D4.anode, D5.anode, C5.1, C6.0, C7.1, D6.anode
  N21: Pico/Pico2_Mod_2.pin_39, D2.cathode
  N22: Pico/Pico2_Mod_3.pin_39, D3.cathode
  N23: D4.cathode, Pico/Pico2_Mod_4.pin_39
  N24: D5.cathode, Pico/Pico2_Mod_5.pin_39

notes:
  Power
  Debug probe
  Server I/O
  Server Board
  Agent 1
  Agent 0
  Agent 2
  Agent 3
  3V3
  5V

custom parts:
  Raspberry Pi Pico or Pico 2: Raspberry Pi Pico and Pico 2. Based around the RP2040 and RP2350 microcontrollers respectively, Picos are low cost microcontroller device bringing Raspberry Pi quality, cost, and easy of use to the microcontroller space. Jan 2021, Split part in to two versions: tht (this one) and SMD. This one will drill holes for a .1 in header in pcb to allow plugging in the module as well as providing pads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
  VGA Adapter Board: VGA adapter board for ECE 4750
